// Logisim project project.circ as structural Verilog: 6 circuits, main circuit main
module main (
  input  in_1,
  input  reset,
  input  in_3,
  output [31:0] INSTRUCTION,
  output [7:0] out_5,
  output [7:0] out_6,
  output [31:0] out_7
);

  wire clk, clock_1_out, uc_1_regw, undriven_3, undriven_4, undriven_5;
  wire [2:0] bit_extender_1_out, bit_extender_2_out, RegEnable, uc_1_x;
  wire [31:0] adder_1_out, adder_2_out, bancoderegistradores_1_rd1, bancoderegistradores_1_rd2, PC_q,
       register_1_q, ula_2_p4, undriven, undriven_2;

  Multiplexer multiplexer_1 (.in0(clock_1_out), .in1(1'b1), .out(clk), .sel(in_1));
  Clock clock_1 (.out(clock_1_out));
  Register #(.width(32)) register_1 (
    .D(adder_1_out), .clk(clk), .Q({register_1_q[31:10], out_6, register_1_q[1:0]}), .clr(in_3));  // open: en
  Adder #(.width(32)) adder_1 (
    .a(32'h4), .b({register_1_q[31:10], out_6, register_1_q[1:0]}), .out(adder_1_out));  // open: cin, cout
  Register #(.width(32)) PC (.D(adder_2_out), .clk(clk), .Q({PC_q[31:10], out_5, PC_q[1:0]}), .clr(reset));  // open: en
  Adder #(.width(32)) adder_2 (.a(32'h4), .b({PC_q[31:10], out_5, PC_q[1:0]}), .out(adder_2_out));  // open: cin, cout
  ROM #(.dataWidth(32)) rom_1 (.addr(out_6), .data(out_7));
  ROM #(.dataWidth(32)) rom_2 (.addr(out_5), .data(INSTRUCTION));
  regCPU regcpu_1 (
    .Clock(clk), .Entry1(out_7[17:13]), .Entry2(out_7[22:18]), .RegEntry(out_7[27:23]), .R1(undriven),
    .R2(undriven_2));  // open: WriteEnable, DataIncome, a0, v0
  UC uc_1 (
    .a(INSTRUCTION[28]), .b(INSTRUCTION[29]), .c(INSTRUCTION[30]), .d(INSTRUCTION[31]), .x(uc_1_x[0]),
    .y(uc_1_x[1]), .z(uc_1_x[2]), .regw(uc_1_regw));
  Bit_Extender #(.in_width(4), .out_width(3)) bit_extender_1 (.in(INSTRUCTION[19:16]), .out(bit_extender_1_out));
  Bit_Extender #(.in_width(4), .out_width(3)) bit_extender_2 (.in(INSTRUCTION[23:20]), .out(bit_extender_2_out));
  Bit_Extender #(.in_width(4), .out_width(3)) bit_extender_3 (.in(INSTRUCTION[27:24]), .out(RegEnable));
  ULA ula_1 (.aluOP(out_7[31:28]), .entry1(undriven), .entry2(undriven_2));  // open: result1, result2
  BancoDeRegistradores bancoderegistradores_1 (
    .READ1(bit_extender_1_out), .READ2(bit_extender_2_out), .clear(undriven_4), .clk(undriven_3),
    .Data(ula_2_p4), .REGEnable(RegEnable), .WriteEnable(uc_1_regw), .RD1(bancoderegistradores_1_rd1),
    .RD2(bancoderegistradores_1_rd2));
  // ULA ula_2: pin names not known; wires that end beside it: bancoderegistradores_1_rd1, bancoderegistradores_1_rd2, RegEnable, ula_2_p4
  RAM #(.dataWidth(32)) ram_1 (.clk(undriven_5), .din(ula_2_p4));  // open: addr, we, oe, dout
  RAM #(.dataWidth(32)) ram_2 (.clk(clk));  // open: addr, we, oe, din, dout

  // Other names for the same wires on the sheet: stop = in_1

  // Notes on the sheet:
  //   contents of rom_1 (hex, n*v repeats v):
  //   10001 10001 10001
  //   contents of rom_2 (hex, n*v repeats v):
  //   10001 10001 10001
endmodule

module ULA (
  input  [3:0] aluOP,
  input  [31:0] entry1,
  input  [31:0] entry2,
  output [31:0] result1,
  output [31:0] result2
);

  wire comparator_2_lt, equal;
  wire [31:0] adder_1_out, and_1_out, bit_extender_1_out, multiplier_1_out, not_1_out, or_1_out, or_2_out,
       shifter_1_out, shifter_2_out, shifter_3_out, subtractor_1_out, xor_1_out;

  Shifter #(.width(32)) shifter_1 (.in(entry1), .\dist (entry2[4:0]), .out(shifter_1_out));
  Shifter #(.shift("ar"), .width(32)) shifter_2 (.in(entry1), .\dist (entry2[4:0]), .out(shifter_2_out));
  Shifter #(.shift("lr"), .width(32)) shifter_3 (.in(entry1), .\dist (entry2[4:0]), .out(shifter_3_out));
  Multiplier #(.width(32)) multiplier_1 (.a(entry1), .b(entry2), .out(multiplier_1_out));  // open: cin, cout
  Adder #(.width(32)) adder_1 (.a(entry1), .b(entry2), .out(adder_1_out));  // open: cin, cout
  Subtractor #(.width(32)) subtractor_1 (.a(entry1), .b(entry2), .out(subtractor_1_out));  // open: bin, bout
  assign and_1_out = entry1 & entry2;  // AND_Gate and_1, 32 bits wide
  assign or_1_out = entry1 | entry2;  // OR_Gate or_1, 32 bits wide
  assign xor_1_out = entry1 ^ entry2;  // XOR_Gate xor_1, 32 bits wide
  assign or_2_out = entry1 | entry2;  // OR_Gate or_2, 32 bits wide
  assign not_1_out = ~or_2_out;  // NOT_Gate not_1, 32 bits wide
  Comparator #(.width(32)) comparator_1 (.a(entry1), .b(entry2));  // open: gt, eq, lt
  Comparator #(.width(32)) comparator_2 (.a(entry1), .b(entry2), .eq(equal), .lt(comparator_2_lt));  // open: gt
  assign bit_extender_1_out = {{31{comparator_2_lt}}, comparator_2_lt};  // Bit_Extender bit_extender_1
  Multiplexer #(.select(4), .width(32)) multiplexer_1 (
    .in0(shifter_1_out), .in1(shifter_2_out), .in2(shifter_3_out), .in3(multiplier_1_out), .in5(adder_1_out),
    .in6(subtractor_1_out), .in7(and_1_out), .in8(or_1_out), .in9(xor_1_out), .in10(not_1_out),
    .in12(bit_extender_1_out), .out(result1), .sel(aluOP));  // open: in4, in11, in13, in14, in15

  // Other names for the same wires on the sheet: entryX[31:0] = entry1; entryY[31:0] = entry2; y5[4:0] = entry2[4:0];
  //   Resul1[31:0] = result1; Resul2[31:0] = result2

  // Notes on the sheet:
  //   OUTPUT
endmodule

module PC (
  input  clk,
  input  reset,
  output [7:0] out_3
);

  wire [31:0] adder_1_out, register_1_q;

  Adder #(.width(32)) adder_1 (
    .a(32'h4), .b({register_1_q[31:10], out_3, register_1_q[1:0]}), .out(adder_1_out));  // open: cin, cout
  Register #(.width(32)) register_1 (
    .D(adder_1_out), .clk(clk), .Q({register_1_q[31:10], out_3, register_1_q[1:0]}), .clr(reset));  // open: en
endmodule

// MUXREG1
module BancoDeRegistradores (
  input  [2:0] READ1,
  input  [2:0] READ2,
  input  clear,
  input  clk,
  input  [31:0] Data,
  input  [2:0] REGEnable,
  input  WriteEnable,
  output [31:0] RD1,
  output [31:0] RD2
);

  wire enaREG0, enaREG1, enaREG2, enaREG3, enaREG4, enaREG5, enaREG6, enaREG7;
  wire [31:0] demultiplexer_1_out0, demultiplexer_1_out1, demultiplexer_1_out2, demultiplexer_1_out3,
       demultiplexer_1_out4, demultiplexer_1_out5, demultiplexer_1_out6, demultiplexer_1_out7, MUXREG0,
       MUXREG1, MUXREG2, MUXREG3, MUXREG4, MUXREG5, MUXREG6, MUXREG7;

  Multiplexer #(.select(3), .width(32)) multiplexer_1 (
    .in0(MUXREG0), .in1(MUXREG1), .in2(MUXREG2), .in3(MUXREG3), .in4(MUXREG4), .in5(MUXREG5), .in6(MUXREG6),
    .in7(MUXREG7), .out(RD1), .sel(READ1));
  Multiplexer #(.select(3), .width(32)) multiplexer_2 (
    .in0(MUXREG0), .in1(MUXREG1), .in2(MUXREG2), .in3(MUXREG3), .in4(MUXREG4), .in5(MUXREG5), .in6(MUXREG6),
    .in7(MUXREG7), .out(RD2), .sel(READ2));
  Demultiplexer #(.select(3), .width(32)) demultiplexer_1 (
    .out0(demultiplexer_1_out0), .out1(demultiplexer_1_out1), .out2(demultiplexer_1_out2),
    .out3(demultiplexer_1_out3), .out4(demultiplexer_1_out4), .out5(demultiplexer_1_out5),
    .out6(demultiplexer_1_out6), .out7(demultiplexer_1_out7), .in(Data), .sel(REGEnable));
  Demultiplexer #(.select(3)) demultiplexer_2 (
    .out0(enaREG0), .out1(enaREG1), .out2(enaREG2), .out3(enaREG3), .out4(enaREG4), .out5(enaREG5),
    .out6(enaREG6), .out7(enaREG7), .in(WriteEnable), .sel(REGEnable));
  Register #(.width(32)) REG0 (.D(demultiplexer_1_out0), .en(enaREG0), .clk(clk), .Q(MUXREG0), .clr(clear));
  Register #(.width(32)) REG1 (.D(demultiplexer_1_out1), .en(enaREG1), .clk(clk), .Q(MUXREG1), .clr(clear));
  Register #(.width(32)) REG2 (.D(demultiplexer_1_out2), .en(enaREG2), .clk(clk), .Q(MUXREG2), .clr(clear));
  Register #(.width(32)) REG3 (.D(demultiplexer_1_out3), .en(enaREG3), .clk(clk), .Q(MUXREG3), .clr(clear));
  Register #(.width(32)) REG4 (.D(demultiplexer_1_out4), .en(enaREG4), .clk(clk), .Q(MUXREG4), .clr(clear));
  Register #(.width(32)) REG5 (.D(demultiplexer_1_out5), .en(enaREG5), .clk(clk), .Q(MUXREG5), .clr(clear));
  Register #(.width(32)) REG6 (.D(demultiplexer_1_out6), .en(enaREG6), .clk(clk), .Q(MUXREG6), .clr(clear));
  Register #(.width(32)) REG7 (.D(demultiplexer_1_out7), .en(enaREG7), .clk(clk), .Q(MUXREG7));  // open: clr
endmodule

module UC (
  input  a,
  input  b,
  input  c,
  input  d,
  output x,
  output y,
  output z,
  output regw
);

  wire and_1_out, and_2_out, and_3_out, and_4_out, and_5_out, and_6_out, and_7_out, and_8_out, and_9_out,
       and_10_out, not_1_out, not_2_out, not_3_out;

  not not_1 (not_1_out, b);
  not not_2 (not_2_out, c);
  not not_3 (not_3_out, d);
  and and_1 (and_1_out, b, not_2_out);
  and and_2 (and_2_out, b, not_3_out);
  and and_3 (and_3_out, not_1_out, c);
  and and_4 (and_4_out, c, not_3_out);
  and and_5 (and_5_out, not_1_out, d);
  and and_6 (and_6_out, not_2_out, d);
  and and_7 (and_7_out, not_1_out, d);
  and and_8 (and_8_out, not_1_out, c);
  and and_9 (and_9_out, b, not_2_out);
  and and_10 (and_10_out, c, not_3_out);
  or or_1 (x, and_1_out, and_2_out);
  or or_2 (y, and_3_out, and_4_out);
  or or_3 (z, and_5_out, and_6_out);
  or or_4 (regw, and_7_out, and_8_out, and_9_out, and_10_out);
endmodule

module regCPU (
  input  WriteEnable,
  input  Clock,
  input  [31:0] DataIncome,
  input  [4:0] Entry1,
  input  [4:0] Entry2,
  input  [4:0] RegEntry,
  input  [31:0] R1,
  input  [31:0] R2,
  input  [31:0] a0,
  input  [31:0] v0
);

  wire demultiplexer_1_out0, demultiplexer_1_out1, demultiplexer_1_out2, demultiplexer_1_out3,
       demultiplexer_2_out0, demultiplexer_2_out1, demultiplexer_2_out2, demultiplexer_2_out3,
       demultiplexer_2_out4, demultiplexer_2_out5, demultiplexer_2_out6, demultiplexer_2_out7,
       demultiplexer_3_out0, demultiplexer_3_out1, demultiplexer_3_out2, demultiplexer_3_out3,
       demultiplexer_3_out4, demultiplexer_3_out5, demultiplexer_3_out6, demultiplexer_3_out7,
       demultiplexer_4_out0, demultiplexer_4_out1, demultiplexer_4_out2, demultiplexer_4_out3,
       demultiplexer_4_out4, demultiplexer_4_out5, demultiplexer_4_out6, demultiplexer_4_out7,
       demultiplexer_5_out0, demultiplexer_5_out1, demultiplexer_5_out2, demultiplexer_5_out3,
       demultiplexer_5_out4, demultiplexer_5_out5, demultiplexer_5_out6, demultiplexer_5_out7, undriven;
  wire [31:0] a1_q, a2_q, a3_q, at_q, azero_q, register_12_q, register_13_q, register_14_q, register_15_q,
       register_16_q, register_17_q, register_18_q, register_19_q, register_20_q, register_21_q,
       register_22_q, register_23_q, register_24_q, register_25_q, register_26_q, register_27_q,
       register_28_q, register_29_q, register_30_q, register_31_q, register_32_q, register_33_q,
       register_34_q, register_35_q, v1_q, vzero_q, zero_q;

  Register #(.width(32)) t0 ();  // open: D, en, Q, clk, clr
  Register #(.width(32)) register_1 ();  // open: D, en, Q, clk, clr
  Register #(.width(32)) t8 ();  // open: D, en, Q, clk, clr
  Register #(.width(32)) t1 ();  // open: D, en, Q, clk, clr
  Register #(.width(32)) register_2 ();  // open: D, en, Q, clk, clr
  Register #(.width(32)) t9 ();  // open: D, en, Q, clk, clr
  Register #(.width(32)) t2 ();  // open: D, en, Q, clk, clr
  Register #(.width(32)) t3 ();  // open: D, en, Q, clk, clr
  Register #(.width(32)) register_3 ();  // open: D, en, Q, clk, clr
  Register #(.width(32)) register_4 ();  // open: D, en, Q, clk, clr
  Register #(.width(32)) register_5 ();  // open: D, en, Q, clk, clr
  Register #(.width(32)) register_6 ();  // open: D, en, Q, clk, clr
  Register #(.width(32)) t4 ();  // open: D, en, Q, clk, clr
  Register #(.width(32)) t5 ();  // open: D, en, Q, clk, clr
  Register #(.width(32)) register_7 (.clr(undriven));  // open: D, en, Q, clk
  Register #(.width(32)) register_8 ();  // open: D, en, Q, clk, clr
  Register #(.width(32)) register_9 ();  // open: D, en, Q, clk, clr
  Register #(.width(32)) sp ();  // open: D, en, Q, clk, clr
  Register #(.width(32)) t6 ();  // open: D, en, Q, clk, clr
  Register #(.width(32)) register_10 ();  // open: D, en, Q, clk, clr
  Register #(.width(32)) fp ();  // open: D, en, Q, clk, clr
  Register #(.width(32)) t7 ();  // open: D, en, Q, clk, clr
  Register #(.width(32)) register_11 ();  // open: D, en, Q, clk, clr
  Register #(.width(32)) ra ();  // open: D, en, Q, clk, clr
  Demultiplexer #(.enable("true"), .select(2)) demultiplexer_1 (
    .out0(demultiplexer_1_out0), .out1(demultiplexer_1_out1), .out2(demultiplexer_1_out2),
    .out3(demultiplexer_1_out3), .in(1'b1), .sel(RegEntry[4:3]), .en(WriteEnable));
  Demultiplexer #(.enable("true"), .select(3)) demultiplexer_2 (
    .out0(demultiplexer_2_out0), .out1(demultiplexer_2_out1), .out2(demultiplexer_2_out2),
    .out3(demultiplexer_2_out3), .out4(demultiplexer_2_out4), .out5(demultiplexer_2_out5),
    .out6(demultiplexer_2_out6), .out7(demultiplexer_2_out7), .in(1'b1), .sel(RegEntry[2:0]),
    .en(demultiplexer_1_out0));
  Demultiplexer #(.enable("true"), .select(3)) demultiplexer_3 (
    .out0(demultiplexer_3_out0), .out1(demultiplexer_3_out1), .out2(demultiplexer_3_out2),
    .out3(demultiplexer_3_out3), .out4(demultiplexer_3_out4), .out5(demultiplexer_3_out5),
    .out6(demultiplexer_3_out6), .out7(demultiplexer_3_out7), .in(1'b1), .sel(RegEntry[2:0]),
    .en(demultiplexer_1_out1));
  Demultiplexer #(.enable("true"), .select(3)) demultiplexer_4 (
    .out0(demultiplexer_4_out0), .out1(demultiplexer_4_out1), .out2(demultiplexer_4_out2),
    .out3(demultiplexer_4_out3), .out4(demultiplexer_4_out4), .out5(demultiplexer_4_out5),
    .out6(demultiplexer_4_out6), .out7(demultiplexer_4_out7), .in(1'b1), .sel(RegEntry[2:0]),
    .en(demultiplexer_1_out2));
  Demultiplexer #(.enable("true"), .select(3)) demultiplexer_5 (
    .out0(demultiplexer_5_out0), .out1(demultiplexer_5_out1), .out2(demultiplexer_5_out2),
    .out3(demultiplexer_5_out3), .out4(demultiplexer_5_out4), .out5(demultiplexer_5_out5),
    .out6(demultiplexer_5_out6), .out7(demultiplexer_5_out7), .in(1'b1), .sel(RegEntry[2:0]),
    .en(demultiplexer_1_out3));
  Register #(.width(32)) zero (.D(DataIncome), .en(demultiplexer_2_out0), .Q(zero_q));  // open: clk, clr
  Register #(.width(32)) register_12 (
    .D(DataIncome), .en(demultiplexer_3_out0), .Q(register_12_q), .clk(Clock));  // open: clr
  Register #(.width(32)) register_13 (
    .D(DataIncome), .en(demultiplexer_4_out0), .Q(register_13_q), .clk(Clock));  // open: clr
  Register #(.width(32)) register_14 (
    .D(DataIncome), .en(demultiplexer_5_out0), .Q(register_14_q), .clk(Clock));  // open: clr
  Register #(.width(32)) at (.D(DataIncome), .en(demultiplexer_2_out1), .Q(at_q), .clk(Clock));  // open: clr
  Register #(.width(32)) register_15 (
    .D(DataIncome), .en(demultiplexer_3_out1), .Q(register_15_q), .clk(Clock));  // open: clr
  Register #(.width(32)) register_16 (
    .D(DataIncome), .en(demultiplexer_4_out1), .Q(register_16_q), .clk(Clock));  // open: clr
  Register #(.width(32)) register_17 (
    .D(DataIncome), .en(demultiplexer_5_out1), .Q(register_17_q), .clk(Clock));  // open: clr
  Register #(.width(32)) vzero (.D(DataIncome), .en(demultiplexer_2_out2), .Q(vzero_q), .clk(Clock));  // open: clr
  Register #(.width(32)) register_18 (
    .D(DataIncome), .en(demultiplexer_3_out2), .Q(register_18_q), .clk(Clock));  // open: clr
  Register #(.width(32)) register_19 (
    .D(DataIncome), .en(demultiplexer_4_out2), .Q(register_19_q), .clk(Clock));  // open: clr
  Register #(.width(32)) register_20 (
    .D(DataIncome), .en(demultiplexer_5_out2), .Q(register_20_q), .clk(Clock));  // open: clr
  Register #(.width(32)) v1 (.D(DataIncome), .en(demultiplexer_2_out3), .Q(v1_q), .clk(Clock));  // open: clr
  Register #(.width(32)) register_21 (
    .D(DataIncome), .en(demultiplexer_3_out3), .Q(register_21_q), .clk(Clock));  // open: clr
  Register #(.width(32)) register_22 (
    .D(DataIncome), .en(demultiplexer_4_out3), .Q(register_22_q), .clk(Clock));  // open: clr
  Register #(.width(32)) register_23 (
    .D(DataIncome), .en(demultiplexer_5_out3), .Q(register_23_q), .clk(Clock));  // open: clr
  Register #(.width(32)) azero (.D(DataIncome), .en(demultiplexer_2_out4), .Q(azero_q), .clk(Clock));  // open: clr
  Register #(.width(32)) register_24 (
    .D(DataIncome), .en(demultiplexer_3_out4), .Q(register_24_q), .clk(Clock));  // open: clr
  Register #(.width(32)) register_25 (
    .D(DataIncome), .en(demultiplexer_4_out4), .Q(register_25_q), .clk(Clock));  // open: clr
  Register #(.width(32)) register_26 (
    .D(DataIncome), .en(demultiplexer_5_out4), .Q(register_26_q), .clk(Clock));  // open: clr
  Register #(.width(32)) a1 (.D(DataIncome), .en(demultiplexer_2_out5), .Q(a1_q), .clk(Clock));  // open: clr
  Register #(.width(32)) register_27 (
    .D(DataIncome), .en(demultiplexer_3_out5), .Q(register_27_q), .clk(Clock));  // open: clr
  Register #(.width(32)) register_28 (
    .D(DataIncome), .en(demultiplexer_4_out5), .Q(register_28_q), .clk(Clock));  // open: clr
  Register #(.width(32)) register_29 (
    .D(DataIncome), .en(demultiplexer_5_out5), .Q(register_29_q), .clk(Clock));  // open: clr
  Register #(.width(32)) a2 (.D(DataIncome), .en(demultiplexer_2_out6), .Q(a2_q), .clk(Clock));  // open: clr
  Register #(.width(32)) register_30 (
    .D(DataIncome), .en(demultiplexer_3_out6), .Q(register_30_q), .clk(Clock));  // open: clr
  Register #(.width(32)) register_31 (
    .D(DataIncome), .en(demultiplexer_4_out6), .Q(register_31_q), .clk(Clock));  // open: clr
  Register #(.width(32)) register_32 (
    .D(DataIncome), .en(demultiplexer_5_out6), .Q(register_32_q), .clk(Clock));  // open: clr
  Register #(.width(32)) a3 (.D(DataIncome), .en(demultiplexer_2_out7), .Q(a3_q), .clk(Clock));  // open: clr
  Register #(.width(32)) register_33 (
    .D(DataIncome), .en(demultiplexer_3_out7), .Q(register_33_q), .clk(Clock));  // open: clr
  Register #(.width(32)) register_34 (
    .D(DataIncome), .en(demultiplexer_4_out7), .Q(register_34_q), .clk(Clock));  // open: clr
  Register #(.width(32)) register_35 (
    .D(DataIncome), .en(demultiplexer_5_out7), .Q(register_35_q), .clk(Clock));  // open: clr
  Multiplexer #(.select(5), .width(32)) multiplexer_1 (
    .in0(zero_q), .in1(at_q), .in2(vzero_q), .in3(v1_q), .in4(azero_q), .in5(a1_q), .in6(a2_q), .in7(a3_q),
    .in8(register_12_q), .in9(register_15_q), .in10(register_18_q), .in11(register_21_q),
    .in12(register_24_q), .in13(register_27_q), .in14(register_30_q), .in15(register_33_q),
    .in16(register_13_q), .in17(register_16_q), .in18(register_19_q), .in19(register_22_q),
    .in20(register_25_q), .in21(register_28_q), .in22(register_31_q), .in23(register_34_q),
    .in24(register_14_q), .in25(register_17_q), .in26(register_20_q), .in27(register_23_q),
    .in28(register_26_q), .in29(register_29_q), .in30(register_32_q), .in31(register_35_q), .out(R1),
    .sel(Entry1));
  Multiplexer #(.select(5), .width(32)) multiplexer_2 (
    .in0(zero_q), .in1(at_q), .in2(vzero_q), .in3(v1_q), .in4(azero_q), .in5(a1_q), .in6(a2_q), .in7(a3_q),
    .in8(register_12_q), .in9(register_15_q), .in10(register_18_q), .in11(register_21_q),
    .in12(register_24_q), .in13(register_27_q), .in14(register_30_q), .in15(register_33_q),
    .in16(register_13_q), .in17(register_16_q), .in18(register_19_q), .in19(register_22_q),
    .in20(register_25_q), .in21(register_28_q), .in22(register_31_q), .in23(register_34_q),
    .in24(register_14_q), .in25(register_17_q), .in26(register_20_q), .in27(register_23_q),
    .in28(register_26_q), .in29(register_29_q), .in30(register_32_q), .in31(register_35_q), .out(R2),
    .sel(Entry2));

  // Other names for the same wires on the sheet: clk = Clock; iReg1[4:0] = Entry1; iReg2[4:0] = Entry2;
  //   reg1[31:0] = R1; reg2[31:0] = R2; we = WriteEnable; a[31:0] = DataIncome; write_data[31:0] = DataIncome;
  //   write_reg[4:0] = RegEntry

  // Notes on the sheet:
  //   OUTPUT
endmodule
